// Digital circuit 4-bit-general-purpose-register.dig as structural Verilog
module _4_bit_general_purpose_register (
  input  [3:0] Address,
  input  clk,
  input  [3:0] Input,
  input  [1:0] CTRL,
  output [3:0] Output_BUS
);

  wire and_1_out, and_2_out, and_3_out, and_4_out, and_5_out, and_6_out, and_7_out, and_8_out, and_9_out,
       and_10_out, and_11_out, and_12_out, and_13_out, and_14_out, and_15_out, and_16_out, decoder_1_out_0,
       decoder_1_out_1, decoder_1_out_2, decoder_1_out_3, decoder_1_out_4, decoder_1_out_5, decoder_1_out_6,
       decoder_1_out_7, decoder_1_out_8, decoder_1_out_9, decoder_1_out_10, decoder_1_out_11,
       decoder_1_out_12, decoder_1_out_13, decoder_1_out_14, decoder_1_out_15;
  wire [3:0] R0_output, R1_output, R2_output, R3_output, R4_output, R5_output, R6_output, R7_output,
       R8_output, R9_output, R10_output, R11_output, R12_output, R13_output, R14_output, R15_output;

  Decoder #(.Selector_Bits(4)) decoder_1 (
    .sel(Address), .out_0(decoder_1_out_0), .out_1(decoder_1_out_1), .out_2(decoder_1_out_2),
    .out_3(decoder_1_out_3), .out_4(decoder_1_out_4), .out_5(decoder_1_out_5), .out_6(decoder_1_out_6),
    .out_7(decoder_1_out_7), .out_8(decoder_1_out_8), .out_9(decoder_1_out_9), .out_10(decoder_1_out_10),
    .out_11(decoder_1_out_11), .out_12(decoder_1_out_12), .out_13(decoder_1_out_13),
    .out_14(decoder_1_out_14), .out_15(decoder_1_out_15));
  and and_1 (and_1_out, clk, decoder_1_out_0);
  and and_2 (and_2_out, clk, decoder_1_out_1);
  and and_3 (and_3_out, clk, decoder_1_out_2);
  and and_4 (and_4_out, clk, decoder_1_out_3);
  and and_5 (and_5_out, clk, decoder_1_out_4);
  and and_6 (and_6_out, clk, decoder_1_out_5);
  and and_7 (and_7_out, clk, decoder_1_out_6);
  and and_8 (and_8_out, clk, decoder_1_out_7);
  and and_9 (and_9_out, clk, decoder_1_out_8);
  and and_10 (and_10_out, clk, decoder_1_out_9);
  and and_11 (and_11_out, clk, decoder_1_out_10);
  and and_12 (and_12_out, clk, decoder_1_out_11);
  and and_13 (and_13_out, clk, decoder_1_out_12);
  and and_14 (and_14_out, clk, decoder_1_out_13);
  and and_15 (and_15_out, clk, decoder_1_out_14);
  and and_16 (and_16_out, clk, decoder_1_out_15);
  _4_Bit_instruction_register R0 (.Clock(and_1_out), .Input(Input), .CTRL(CTRL), .Output(R0_output));
  _4_Bit_instruction_register R1 (.Clock(and_2_out), .Input(Input), .CTRL(CTRL), .Output(R1_output));
  _4_Bit_instruction_register R2 (.Clock(and_3_out), .Input(Input), .CTRL(CTRL), .Output(R2_output));
  _4_Bit_instruction_register R3 (.Clock(and_4_out), .Input(Input), .CTRL(CTRL), .Output(R3_output));
  _4_Bit_instruction_register R4 (.Clock(and_5_out), .Input(Input), .CTRL(CTRL), .Output(R4_output));
  _4_Bit_instruction_register R5 (.Clock(and_6_out), .Input(Input), .CTRL(CTRL), .Output(R5_output));
  _4_Bit_instruction_register R6 (.Clock(and_7_out), .Input(Input), .CTRL(CTRL), .Output(R6_output));
  _4_Bit_instruction_register R7 (.Clock(and_8_out), .Input(Input), .CTRL(CTRL), .Output(R7_output));
  _4_Bit_instruction_register R8 (.Clock(and_9_out), .Input(Input), .CTRL(CTRL), .Output(R8_output));
  _4_Bit_instruction_register R9 (.Clock(and_10_out), .Input(Input), .CTRL(CTRL), .Output(R9_output));
  _4_Bit_instruction_register R10 (.Clock(and_11_out), .Input(Input), .CTRL(CTRL), .Output(R10_output));
  _4_Bit_instruction_register R11 (.Clock(and_12_out), .Input(Input), .CTRL(CTRL), .Output(R11_output));
  _4_Bit_instruction_register R12 (.Clock(and_13_out), .Input(Input), .CTRL(CTRL), .Output(R12_output));
  _4_Bit_instruction_register R13 (.Clock(and_14_out), .Input(Input), .CTRL(CTRL), .Output(R13_output));
  _4_Bit_instruction_register R14 (.Clock(and_15_out), .Input(Input), .CTRL(CTRL), .Output(R14_output));
  _4_Bit_instruction_register R15 (.Clock(and_16_out), .Input(Input), .CTRL(CTRL), .Output(R15_output));
  Multiplexer #(.Selector_Bits(4), .Bits(4)) multiplexer_1 (
    .sel(Address), .in_0(R0_output), .in_1(R1_output), .in_2(R2_output), .in_3(R3_output), .in_4(R4_output),
    .in_5(R5_output), .in_6(R6_output), .in_7(R7_output), .in_8(R8_output), .in_9(R9_output),
    .in_10(R10_output), .in_11(R11_output), .in_12(R12_output), .in_13(R13_output), .in_14(R14_output),
    .in_15(R15_output), .out(Output_BUS));
endmodule
