// Digital circuit Register-File-3-19.dig as structural Verilog
module Register_File_3_19 (
  input  [1:0] Select_read1,
  input  [1:0] Select_read2,
  input  clk,
  input  [3:0] Write_data,
  input  [1:0] Select_write,
  input  [7:0] ctrl_registers,
  output [3:0] Read_data_1,
  output [3:0] Read_data_2
);

  wire [3:0] demultiplexer_1_out_0, demultiplexer_1_out_1, demultiplexer_1_out_2, demultiplexer_1_out_3,
       R0_output, R1_output, R2_output, R3_output;

  Demultiplexer #(.Bits(4), .Selector_Bits(2)) demultiplexer_1 (
    .sel(Select_write), .in(Write_data), .out_0(demultiplexer_1_out_0), .out_1(demultiplexer_1_out_1),
    .out_2(demultiplexer_1_out_2), .out_3(demultiplexer_1_out_3));
  _4_Bit_instruction_register R0 (
    .Clock(clk), .Input(demultiplexer_1_out_0), .CTRL(ctrl_registers[1:0]), .Output(R0_output));
  _4_Bit_instruction_register R1 (
    .Clock(clk), .Input(demultiplexer_1_out_1), .CTRL(ctrl_registers[3:2]), .Output(R1_output));
  _4_Bit_instruction_register R2 (
    .Clock(clk), .Input(demultiplexer_1_out_2), .CTRL(ctrl_registers[5:4]), .Output(R2_output));
  _4_Bit_instruction_register R3 (
    .Clock(clk), .Input(demultiplexer_1_out_3), .CTRL(ctrl_registers[7:6]), .Output(R3_output));
  Multiplexer #(.Bits(4), .Selector_Bits(2)) multiplexer_1 (
    .sel(Select_read1), .in_0(R0_output), .in_1(R1_output), .in_2(R2_output), .in_3(R3_output),
    .out(Read_data_1));
  Multiplexer #(.Selector_Bits(2), .Bits(4)) multiplexer_2 (
    .sel(Select_read2), .in_0(R0_output), .in_1(R1_output), .in_2(R2_output), .in_3(R3_output),
    .out(Read_data_2));
endmodule
