// Digital circuit data-path-4-bit-processor-3-24.dig as structural Verilog
module data_path_4_bit_processor_3_24 (
  input  clk,
  input  [1:0] IR_ctrl,
  input  [1:0] Mem_ctrl,
  input  [3:0] Mem_Input,
  output [1:0] PC_Output,
  output [15:0] Instructions_16_bit,
  output [3:0] ALU_out,
  output [3:0] data_1_out,
  output [3:0] data_2_out
);

  wire [7:0] registerfile_write_ctrl_2_26_1_write_ctrl;

  // instr_mem_module_3_24 instr_mem_module_3_24_1: pin names not known; wires that end beside it: IR_ctrl, 2'b01, Mem_ctrl, Mem_Input, clk, Instructions_16_bit, PC_Output
  Register_File_3_19 register_file_3_19_1 (
    .Select_read1(Instructions_16_bit[5:4]), .Select_read2(Instructions_16_bit[3:2]), .clk(clk),
    .Write_data(ALU_out), .Select_write(Instructions_16_bit[1:0]),
    .ctrl_registers(registerfile_write_ctrl_2_26_1_write_ctrl), .Read_data_1(data_1_out),
    .Read_data_2(data_2_out));
  registerfile_write_ctrl_2_26 registerfile_write_ctrl_2_26_1 (
    .Opcode3(Instructions_16_bit[1:0]), .Write_ctrl(registerfile_write_ctrl_2_26_1_write_ctrl));
  ALU_3_19 alu_3_19_1 (
    .A(data_1_out), .B(data_2_out), .S_1_S_0_C_in(Instructions_16_bit[8:6]), .D(ALU_out));  // open: Overflow
endmodule

/* Test case Test Circuit:
IR-ctrl Mem-ctrl Mem-Input clk PC-Output Instructions-16-bit ALU-out data-1-out  data-2-out
0 1 1 c x x x x x
0 1 2 c x x x x x
0 1 3 c x x x x x
0 1 4 c x x x x x
0 1 5 c x x x x x 
0 1 6 c x x x x x 
0 1 7 c x x x x x
0 1 8 c x x x x x
1 0 1 c x x x x x
1 0 1 c x x x x x
1 0 1 c x x x x x
1 0 1 c x x x x x
1 0 1 c x x x x x
1 0 1 c x x x x x
1 0 1 c x x x x x
1 0 1 c x x x x x
*/
