// Digital circuit instr-mem-module-3-24.dig as structural Verilog
module instr_mem_module_3_24 (
  input  [1:0] IR_ctrl,
  input  [1:0] pc_ctrl,
  input  [1:0] intr_mem_ctrl,
  input  [3:0] instr_mem_input,
  input  clk,
  output [15:0] ir_output,
  output [3:0] pc_output
);

  wire and_1_out, not_1_out, not_2_out;
  wire [1:0] demultiplexer_1_out_0, demultiplexer_1_out_1, demultiplexer_1_out_2, demultiplexer_1_out_3;
  wire [3:0] _4_bit_general_purpose_register_1_output_bus, _4_bit_instruction_register_1_output,
       _4_bit_instruction_register_2_output, _4_bit_instruction_register_3_output,
       _4_bit_instruction_register_4_output, demultiplexer_2_out_0, demultiplexer_2_out_1,
       demultiplexer_2_out_2, demultiplexer_2_out_3;

  _4_Bit_Program_Counter _4_bit_program_counter_1 (.Clock(clk), .CTRL(pc_ctrl), .Output(pc_output));
  _4_bit_general_purpose_register _4_bit_general_purpose_register_1 (
    .Address(pc_output), .clk(clk), .Input(instr_mem_input), .CTRL(intr_mem_ctrl),
    .Output_BUS(_4_bit_general_purpose_register_1_output_bus));
  Demultiplexer #(.Selector_Bits(2), .Bits(2)) demultiplexer_1 (
    .sel(pc_output[1:0]), .in(IR_ctrl), .out_0(demultiplexer_1_out_0), .out_1(demultiplexer_1_out_1),
    .out_2(demultiplexer_1_out_2), .out_3(demultiplexer_1_out_3));
  Demultiplexer #(.Selector_Bits(2), .Bits(4)) demultiplexer_2 (
    .sel(pc_output[1:0]), .in(_4_bit_general_purpose_register_1_output_bus), .out_0(demultiplexer_2_out_0),
    .out_1(demultiplexer_2_out_1), .out_2(demultiplexer_2_out_2), .out_3(demultiplexer_2_out_3));
  _4_Bit_instruction_register _4_bit_instruction_register_1 (
    .Clock(clk), .Input(demultiplexer_2_out_0), .CTRL(demultiplexer_1_out_0),
    .Output(_4_bit_instruction_register_1_output));
  _4_Bit_instruction_register _4_bit_instruction_register_2 (
    .Clock(clk), .Input(demultiplexer_2_out_1), .CTRL(demultiplexer_1_out_1),
    .Output(_4_bit_instruction_register_2_output));
  _4_Bit_instruction_register _4_bit_instruction_register_3 (
    .Clock(clk), .Input(demultiplexer_2_out_2), .CTRL(demultiplexer_1_out_2),
    .Output(_4_bit_instruction_register_3_output));
  _4_Bit_instruction_register _4_bit_instruction_register_4 (
    .Clock(clk), .Input(demultiplexer_2_out_3), .CTRL(demultiplexer_1_out_3),
    .Output(_4_bit_instruction_register_4_output));
  assign ir_output = and_1_out ? {_4_bit_instruction_register_4_output, _4_bit_instruction_register_3_output, _4_bit_instruction_register_2_output, _4_bit_instruction_register_1_output} : 16'bz;  // Driver driver_1
  not not_1 (not_1_out, pc_output[0]);
  not not_2 (not_2_out, pc_output[1]);
  and and_1 (and_1_out, not_1_out, not_2_out);
endmodule
